# Fritzing sketch Schematic (saved by Fritzing 0.9.3b)
breadboards: 1

parts:
  R1 = Resistor [tolerance=±5% resistance=220 package=THT]
  R2 = Resistor [tolerance=±5% resistance=220 package=THT]
  R3 = Resistor [tolerance=±5% resistance=220 package=THT]
  LED1 = LED - 5mm [color="Red (633nm)" package="5 mm [THT]"]
  LED2 = LED - 5mm [color="Red (633nm)" package="5 mm [THT]"]
  LED3 = LED - 5mm [color="Red (633nm)" package="5 mm [THT]"]
  J1 = Basic Servo
  J2 = Basic Servo
  VCC1 = 4 x AAA Battery Mount
  Componente1 = Arduino Uno (Rev3)
  Raspberry_Pi1 = Raspberry Pi B rev2
  R4 = Resistor [tolerance=±5% resistance=100k package=THT]
  R5 = Resistor [tolerance=±5% resistance=150k package=THT]
  VCC2 = 4 x AAA Battery Mount

nets:
  N1: R1.Pin_0, LED1.anode
  N2: R1.Pin_1, Raspberry_Pi1.GPIO_4
  N3: R2.Pin_0, LED3.anode
  N4: R2.Pin_1, Raspberry_Pi1.GPIO_27
  N5: R3.Pin_0, LED2.anode
  N6: R3.Pin_1, Raspberry_Pi1.GPIO_22
  GND: LED1.cathode, J1.gnd, VCC1.-, Componente1.GND, Raspberry_Pi1.GND, R4.Pin_0, VCC2.-
  VCC: J1.vcc, J2.vcc, VCC1.+, R5.Pin_1
  N7: J1.pulse, Componente1.D9_PWM
  N8: J2.pulse, Componente1.D10_PWM/SS
  N9: Componente1.A4/SDA, Raspberry_Pi1.GPIO_2
  N10: Componente1.A5/SCL, Raspberry_Pi1.GPIO_3
  N11: Componente1.VIN, VCC2.+
  N12: Raspberry_Pi1.GPIO_23, R4.Pin_1, R5.Pin_0
